# Fritzing sketch schematics (saved by Fritzing 0.9.3b)
breadboards: 1

parts:
  Raspberry_Pi_1 = Raspberry Pi 3 [part_number=RPI-3-V1.2]
  Relay_on_channel_1 = RELAY [package=relay-jzc]
  Relay_on_channel_2 = RELAY [package=relay-jzc]
  LED_reflector_230V = LCD_BACKLIGHT_PADS [package=lcd_backlight_pads]
  230V_AC_power_source = Power plug
  J1 = Piezo Speaker
  PIR_module_HC-SR501 = HC-SR501 Body Sensor Module

nets:
  N1: Raspberry_Pi_1.GPIO17, PIR_module_HC-SR501.OUT
  N2: Raspberry_Pi_1.GPIO26, Relay_on_channel_1.COIL1
  N3: Raspberry_Pi_1.GPIO20, Relay_on_channel_2.COIL1
  GND: Raspberry_Pi_1.GND, Relay_on_channel_1.COIL2, Relay_on_channel_2.COIL2, J1.pin1, PIR_module_HC-SR501.GND
  5V: Raspberry_Pi_1.5V, Relay_on_channel_2.MAIN, PIR_module_HC-SR501.VCC
  N4: Relay_on_channel_1.NO, LED_reflector_230V.K
  N5: Relay_on_channel_1.MAIN, 230V_AC_power_source.VCC
  N6: Relay_on_channel_2.NO, J1.pin2
  N7: LED_reflector_230V.A, 230V_AC_power_source.GND

custom parts:
  HC-SR501 Body Sensor Module: Pyroelectric Infrared PIR Motion Sensor Detector Module
